# Fritzing sketch RGB_LED (saved by Fritzing 0.9.0b)
breadboards: 1

parts:
  12V = screw terminal, 2 pins
  J9 = screw terminal, 2 pins [part_number=LEDR1]
  IC1 = Optocoupler [package=THT]
  J10 = screw terminal, 2 pins [part_number=LEDG1]
  IC2 = Optocoupler [package=THT]
  R2 = Resistor [tolerance=±5% resistance=220 package=THT]
  J11 = screw terminal, 2 pins [part_number=LEDB1]
  IC3 = Optocoupler [package=THT]
  R3 = Resistor [tolerance=±5% resistance=220 package=THT]
  J12 = screw terminal, 2 pins [part_number=LEDR2]
  IC4 = Optocoupler [package=THT]
  R4 = Resistor [tolerance=±5% resistance=220 package=THT]
  J13 = screw terminal, 2 pins [part_number=LEDG2]
  IC5 = Optocoupler [package=THT]
  R5 = Resistor [tolerance=±5% resistance=220 package=THT]
  J14 = screw terminal, 2 pins [part_number=LEDB2]
  IC6 = Optocoupler [package=THT]
  R6 = Resistor [tolerance=±5% resistance=220 package=THT]
  J15 = screw terminal, 2 pins [part_number=LEDR3]
  IC7 = Optocoupler [package=THT]
  R7 = Resistor [tolerance=±5% resistance=220 package=THT]
  J16 = screw terminal, 2 pins [part_number=LEDG3]
  IC8 = Optocoupler [package=THT]
  R8 = Resistor [tolerance=±5% resistance=220 package=THT]
  J17 = screw terminal, 2 pins [part_number=LEDB3]
  IC9 = Optocoupler [package=THT]
  R9 = Resistor [tolerance=±5% resistance=220 package=THT]
  R1 = Resistor [tolerance=±5% resistance=220 package=THT]
  J1 = Generic shrouded header - 10 pins [form="♂ (shrouded male)" package=THT]

nets:
  N1: 12V.pin1, J9.pin2, J10.pin2, J11.pin2, J12.pin2, J13.pin2, J14.pin2, J15.pin2, J16.pin2, J17.pin2
  N2: 12V.pin2, IC1.Pin_4, IC2.Pin_4, IC3.Pin_4, IC4.Pin_4, IC5.Pin_4, IC6.Pin_4, IC7.Pin_4, IC8.Pin_4, IC9.Pin_4
  N3: J9.pin1, IC1.Pin_5
  N4: IC1.Pin_1, R1.Pin_1
  N5: IC1.Pin_2, IC2.Pin_2, IC3.Pin_2, IC4.Pin_2, IC5.Pin_2, IC6.Pin_2, IC7.Pin_2, IC8.Pin_2, IC9.Pin_2, J1.pin1
  N6: J10.pin1, IC2.Pin_5
  N7: IC2.Pin_1, R2.Pin_1
  N8: R2.Pin_0, J1.pin3
  N9: J11.pin1, IC3.Pin_5
  N10: IC3.Pin_1, R3.Pin_1
  N11: R3.Pin_0, J1.pin4
  N12: J12.pin1, IC4.Pin_5
  N13: IC4.Pin_1, R4.Pin_1
  N14: R4.Pin_0, J1.pin5
  N15: J13.pin1, IC5.Pin_5
  N16: IC5.Pin_1, R5.Pin_1
  N17: R5.Pin_0, J1.pin6
  N18: J14.pin1, IC6.Pin_5
  N19: IC6.Pin_1, R6.Pin_1
  N20: R6.Pin_0, J1.pin7
  N21: J15.pin1, IC7.Pin_5
  N22: IC7.Pin_1, R7.Pin_1
  N23: R7.Pin_0, J1.pin8
  N24: J16.pin1, IC8.Pin_5
  N25: IC8.Pin_1, R8.Pin_1
  N26: R8.Pin_0, J1.pin9
  N27: J17.pin1, IC9.Pin_5
  N28: IC9.Pin_1, R9.Pin_1
  N29: R9.Pin_0, J1.pin10
  N30: R1.Pin_0, J1.pin2

custom parts:
  Generic shrouded header - 10 pins: Generic shrouded header
