# Fritzing sketch RGB_LED_kupferfüllung (saved by Fritzing 0.9.0b)
circuit board: 8.46667cm x 5.64444cm
breadboards: 1

parts:
  12V = screw terminal, 2 pins
  JR1 = screw terminal, 2 pins [part_number=LEDR1]
  IC1 = Optocoupler [package=THT]
  JG1 = screw terminal, 2 pins [part_number=LEDG1]
  IC2 = Optocoupler [package=THT]
  R2 = Resistor [tolerance=±5% resistance=220 package=THT]
  JB1 = screw terminal, 2 pins [part_number=LEDB1]
  IC3 = Optocoupler [package=THT]
  R3 = Resistor [tolerance=±5% resistance=220 package=THT]
  JR2 = screw terminal, 2 pins [part_number=LEDR2]
  IC4 = Optocoupler [package=THT]
  R4 = Resistor [tolerance=±5% resistance=220 package=THT]
  JG2 = screw terminal, 2 pins [part_number=LEDG2]
  IC5 = Optocoupler [package=THT]
  R5 = Resistor [tolerance=±5% resistance=220 package=THT]
  JB2 = screw terminal, 2 pins [part_number=LEDB2]
  IC6 = Optocoupler [package=THT]
  R6 = Resistor [tolerance=±5% resistance=220 package=THT]
  JR3 = screw terminal, 2 pins [part_number=LEDR3]
  IC7 = Optocoupler [package=THT]
  R7 = Resistor [tolerance=±5% resistance=220 package=THT]
  JG3 = screw terminal, 2 pins [part_number=LEDG3]
  IC8 = Optocoupler [package=THT]
  R8 = Resistor [tolerance=±5% resistance=220 package=THT]
  JB3 = screw terminal, 2 pins [part_number=LEDB3]
  IC9 = Optocoupler [package=THT]
  R9 = Resistor [tolerance=±5% resistance=220 package=THT]
  R1 = Resistor [tolerance=±5% resistance=220 package=THT]
  J1 = con0000 [form="♂ (shrouded male)"]

nets:
  N1: 12V.pin1, JR1.pin2, JG1.pin2, JB1.pin2, JR2.pin2, JG2.pin2, JB2.pin2, JR3.pin2, JG3.pin2, JB3.pin2
  N2: 12V.pin2, IC1.Pin_4, IC2.Pin_4, IC3.Pin_4, IC4.Pin_4, IC5.Pin_4, IC6.Pin_4, IC7.Pin_4, IC8.Pin_4, IC9.Pin_4
  N3: JR1.pin1, IC1.Pin_5
  N4: IC1.Pin_1, R1.Pin_1
  N5: IC1.Pin_2, IC2.Pin_2, IC3.Pin_2, IC4.Pin_2, IC5.Pin_2, IC6.Pin_2, IC7.Pin_2, IC8.Pin_2, IC9.Pin_2, J1.connector0
  N6: JG1.pin1, IC2.Pin_5
  N7: IC2.Pin_1, R2.Pin_1
  N8: R2.Pin_0, J1.connector1
  N9: JB1.pin1, IC3.Pin_5
  N10: IC3.Pin_1, R3.Pin_1
  N11: R3.Pin_0, J1.connector8
  N12: JR2.pin1, IC4.Pin_5
  N13: IC4.Pin_1, R4.Pin_1
  N14: R4.Pin_0, J1.connector2
  N15: JG2.pin1, IC5.Pin_5
  N16: IC5.Pin_1, R5.Pin_1
  N17: R5.Pin_0, J1.connector7
  N18: JB2.pin1, IC6.Pin_5
  N19: IC6.Pin_1, R6.Pin_1
  N20: R6.Pin_0, J1.connector3
  N21: JR3.pin1, IC7.Pin_5
  N22: IC7.Pin_1, R7.Pin_1
  N23: R7.Pin_0, J1.connector6
  N24: JG3.pin1, IC8.Pin_5
  N25: IC8.Pin_1, R8.Pin_1
  N26: R8.Pin_0, J1.connector4
  N27: JB3.pin1, IC9.Pin_5
  N28: IC9.Pin_1, R9.Pin_1
  N29: R9.Pin_0, J1.connector5
  N30: R1.Pin_0, J1.connector9

notes:
  omnibot.de
