# Fritzing sketch RGB_LED_kupferfüllung3 (saved by Fritzing 0.9.0b)
circuit board: 8.46667cm x 5.64444cm
breadboards: 1

parts:
  IC1 = Optocoupler [package=THT]
  IC2 = Optocoupler [package=THT]
  R2 = Resistor [tolerance=±5% resistance=220 package=THT]
  IC3 = Optocoupler [package=THT]
  R3 = Resistor [tolerance=±5% resistance=220 package=THT]
  IC4 = Optocoupler [package=THT]
  R4 = Resistor [tolerance=±5% resistance=220 package=THT]
  IC5 = Optocoupler [package=THT]
  R5 = Resistor [tolerance=±5% resistance=220 package=THT]
  IC6 = Optocoupler [package=THT]
  R6 = Resistor [tolerance=±5% resistance=220 package=THT]
  IC7 = Optocoupler [package=THT]
  R7 = Resistor [tolerance=±5% resistance=220 package=THT]
  IC8 = Optocoupler [package=THT]
  R8 = Resistor [tolerance=±5% resistance=220 package=THT]
  IC9 = Optocoupler [package=THT]
  R9 = Resistor [tolerance=±5% resistance=220 package=THT]
  R1 = Resistor [tolerance=±5% resistance=220 package=THT]
  J1 = shrouded pin header, 10 pins [form="♂ (shrouded male)"]
  JR2 = screw terminal, 2 pins
  JR3 = screw terminal, 2 pins
  JG3 = screw terminal, 2 pins
  JB3 = screw terminal, 2 pins
  JB2 = screw terminal, 2 pins
  JG2 = screw terminal, 2 pins
  JB1 = screw terminal, 2 pins
  JG1 = screw terminal, 2 pins
  JR1 = screw terminal, 2 pins
  12V = screw terminal, 2 pins

nets:
  N1: IC1.Pin_1, R1.Pin_1
  N2: IC1.Pin_2, IC2.Pin_2, IC3.Pin_2, IC4.Pin_2, IC5.Pin_2, IC6.Pin_2, IC7.Pin_2, IC8.Pin_2, IC9.Pin_2, J1.pin1
  N3: IC1.Pin_4, IC2.Pin_4, IC3.Pin_4, IC4.Pin_4, IC5.Pin_4, IC6.Pin_4, IC7.Pin_4, IC8.Pin_4, IC9.Pin_4, 12V.pin2
  N4: IC1.Pin_5, JR1.pin1
  N5: IC2.Pin_1, R2.Pin_1
  N6: IC2.Pin_5, JG1.pin1
  N7: R2.Pin_0, J1.pin2
  N8: IC3.Pin_1, R3.Pin_1
  N9: IC3.Pin_5, JB1.pin1
  N10: R3.Pin_0, J1.pin9
  N11: IC4.Pin_1, R4.Pin_1
  N12: IC4.Pin_5, JR2.pin1
  N13: R4.Pin_0, J1.pin3
  N14: IC5.Pin_1, R5.Pin_1
  N15: IC5.Pin_5, JG2.pin1
  N16: R5.Pin_0, J1.pin8
  N17: IC6.Pin_1, R6.Pin_1
  N18: IC6.Pin_5, JB2.pin1
  N19: R6.Pin_0, J1.pin4
  N20: IC7.Pin_1, R7.Pin_1
  N21: IC7.Pin_5, JR3.pin1
  N22: R7.Pin_0, J1.pin7
  N23: IC8.Pin_1, R8.Pin_1
  N24: IC8.Pin_5, JG3.pin1
  N25: R8.Pin_0, J1.pin5
  N26: IC9.Pin_1, R9.Pin_1
  N27: IC9.Pin_5, JB3.pin1
  N28: R9.Pin_0, J1.pin6
  N29: R1.Pin_0, J1.pin10
  N30: JR2.pin2, JR3.pin2, JG3.pin2, JB3.pin2, JB2.pin2, JG2.pin2, JB1.pin2, JG1.pin2, JR1.pin2, 12V.pin1

notes:
  omnibot.de
  direcs.de
